# Fritzing sketch Fritzing_CelestronESPWifi (saved by Fritzing 0.9.5d)

parts:
  RJ12 = RJ11 Jack [package=rj11-6]
  U1 = ESP-12F (ESP8266 WiFi Module) [part_number=ESP8266]
  10K = Resistor [tolerance=±5% resistance=10000 package="2010 [SMD]"]
  M1 = RioRand LM2596
  D1 = Diode [package=diode-hv]
  D2 = Diode [package=diode-hv]

nets:
  N1: RJ12.1, U1.GPIO2
  N2: RJ12.2, M1.Pin_2
  N3: RJ12.3, D1.A, D2.C
  N4: RJ12.4, M1.Pin_1
  N5: U1.VCC, 10K.Pin_1, M1.Pin_3
  N6: U1.EN, 10K.Pin_0
  N7: U1.GND, U1.GPIO15, M1.Pin_4
  N8: U1.GPIO4, D2.A
  N9: U1.GPIO5, D1.C

custom parts:
  ESP-12F (ESP8266 WiFi Module): WiFi Module based on the ESP8266 with onboard PCB antenna and UART communications
